# Fritzing sketch Part4Prelab (saved by Fritzing 0.9.3b)
perfboards: 2

parts:
  IC1 = Voltage Regulator [package=to220-igo]
  C1 = Capacitor [package=cap-pth-large]
  C2 = Capacitor [package=cap-pth-large]
  U3 = OP482 - Low Power, High Speed JFET Quad Operational Amplifier [part_number=OP482]  # not connected
  U4 = OP482 - Low Power, High Speed JFET Quad Operational Amplifier [part_number=OP482]  # not connected
  U6 = OP482 - Low Power, High Speed JFET Quad Operational Amplifier [part_number=OP482]  # not connected
  U7 = OP482 - Low Power, High Speed JFET Quad Operational Amplifier [part_number=OP482]  # not connected
  R1 = 10k Ω Resistor [package=THT]
  R2 = Resistor [tolerance=±5% resistance=220 package=THT]  # not connected
  R3 = Resistor [tolerance=±5% resistance=220 package="1206 [SMD]"]
  R4 = Resistor [tolerance=±5% resistance=220 package="0805 [SMD]"]
  Q1 = LTR-301 [package=ltr-301]  # not connected
  D1 = Rectifier Diode 10A [part_number=P1000K]
  U1 = OP482 - Low Power, High Speed JFET Quad Operational Amplifier [part_number=OP482]
  U8 = OP482 - Low Power, High Speed JFET Quad Operational Amplifier [part_number=OP482]  # not connected
  U9 = OP482 - Low Power, High Speed JFET Quad Operational Amplifier [part_number=OP482]  # not connected
  U10 = OP482 - Low Power, High Speed JFET Quad Operational Amplifier [part_number=OP482]  # not connected
  U11 = OP482 - Low Power, High Speed JFET Quad Operational Amplifier [part_number=OP482]  # not connected
  IC2 = Voltage Regulator [package=to220-igo]  # not connected

nets:
  N1: IC1.GND, C2.2
  N2: IC1.OUT, R1.Pin_0, R3.Pin_1, D1.anode, U1.+IND
  N3: C1.2, D1.cathode
  N4: C2.1, R1.Pin_1
  N5: R4.Pin_0, U1.-INA
  N6: R4.Pin_1, U1.OUTA

custom parts:
  10k Ω Resistor: A generic resistor (0.25W)
